# Fritzing sketch ESP-32-OFFLINE-VOICE-RECOGNITION (saved by Fritzing 0.9.3b)
breadboards: 1

parts:
  M1 = ESP32-S3-DevKitC-1-N8R8-v1 [part_number=ESP32-S3-DevKitC-1-N8R8-v1]
  Part1 = INMP441
  LED1 = LED - 3mm [color="Red (633nm)" package="3 mm [THT]"]
  LED2 = LED - 3mm [color="Red (633nm)" package="3 mm [THT]"]
  LED3 = LED - 3mm [color="Red (633nm)" package="3 mm [THT]"]
  LED4 = LED - 3mm [color="Red (633nm)" package="3 mm [THT]"]

nets:
  N1: M1.pin_1, M1.pin_2, Part1.VDD
  N2: M1.pin_4, LED3.anode
  N3: M1.pin_5, LED2.anode
  N4: M1.pin_6, LED1.anode
  N5: M1.pin_7, LED4.anode
  N6: M1.pin_16, Part1.SD
  N7: M1.pin_17, Part1.WS
  N8: M1.pin_18, Part1.SCK
  N9: M1.pin_22, M1.pin_23, M1.pin_24, M1.pin_44, Part1.L/R, Part1.GND, LED1.cathode, LED2.cathode, LED3.cathode, LED4.cathode

custom parts:
  ESP32-S3-DevKitC-1-N8R8-v1: ESP32-S3-DevKitC-1-N8R8-v1 This module is 44pins long (2x22) and 11 pins width.
  INMP441: This is a simple breakout board for the INMP441 I2S MEMS microphone.
